# Fritzing sketch IMUSketch (saved by Fritzing 0.9.2b)
breadboards: 1

parts:
  Part1 = Arduino Nano (Rev3.0)
  Part2 = Bluetooth HC-05 Macho
  GY1 = MPU-6050 Board GY-521 [form="♀ (female)" package=THT]

nets:
  N1: Part1.D1/TX, Part2.RXD
  N2: Part1.D0/RX, Part2.TXD
  GND: Part1.GND, Part2.GND, GY1.pin2
  N3: Part1.D2, GY1.pin8
  5V: Part1.5V, Part2.VCC, GY1.pin1
  N4: Part1.A5, GY1.pin3
  N5: Part1.A4, GY1.pin4

custom parts:
  MPU-6050 Board GY-521: Acelerometro y Giroscopio MPU-6050 Board GY-521
