# Fritzing sketch JoySketch (saved by Fritzing 0.9.2b)

parts:
  Part1 = Arduino Pro Mini v13
  Part2 = Thumb Joystick
  U1 = LIPO-110mAh [package=lipo-110]
  S1 = Pushbutton [package="[THT]"]
  S2 = Pushbutton [package="[THT]"]  # not connected
  Part3 = Bluetooth HC-05 Macho

nets:
  N1: Part1.D0/TX, Part3.RXD
  N2: Part1.D1/RX, Part3.TXD
  VCC: Part1.VCC, Part2.VCC, Part3.VCC
  GND: Part1.GND, U1.-, Part3.GND
  N3: Part1.RAW, U1.+
  N4: Part1.A3, S1.Pin_3, S1.Pin_4
  N5: Part1.A2, Part2.SEL
  N6: Part1.A1, Part2.HORZ
  N7: Part1.A0, Part2.VERT

notes:
  VR Joystick
  Notes:
  -2nd Button Not pluged in
  -Code in Github
